// Logisim project ALU.circ as structural Verilog: 5 circuits, main circuit main
module main (
  input  Operation,
  input  A,
  input  B,
  output out_4
);

  wire and_1_out, or_1_out;

  and and_1 (and_1_out, A, B);
  or or_1 (or_1_out, A, B);
  _2_1_MUX u_2_1_mux_1 (.in_0(and_1_out), .in_1(or_1_out), .Select(Operation), .out(out_4));

  // Notes on the sheet:
  //   1-Bit ALU Version 1
  //   Iho López Tobi
  //   July 1st 2019
endmodule

module _1_Bit_Adder (
  input  Carry_in,
  input  A,
  input  B,
  output Sum,
  output Carry_out
);

  wire and_1_out, and_2_out, and_3_out, and_4_out, and_5_out, and_6_out, and_7_out, not_1_out, not_2_out,
       not_3_out, not_4_out, not_5_out, not_6_out, not_7_out, not_8_out, not_9_out;

  not not_1 (not_1_out, A);
  not not_2 (not_2_out, B);
  and and_1 (and_1_out, not_1_out, not_2_out, Carry_in);
  not not_3 (not_3_out, A);
  and and_2 (and_2_out, not_3_out, B, not_4_out);
  not not_4 (not_4_out, Carry_in);
  not not_5 (not_5_out, A);
  and and_3 (and_3_out, not_5_out, B, Carry_in);
  and and_4 (and_4_out, A, not_6_out, not_7_out);
  not not_6 (not_6_out, B);
  not not_7 (not_7_out, Carry_in);
  and and_5 (and_5_out, A, not_8_out, Carry_in);
  not not_8 (not_8_out, B);
  and and_6 (and_6_out, A, B, not_9_out);
  not not_9 (not_9_out, Carry_in);
  and and_7 (and_7_out, A, B, Carry_in);
  or or_1 (Carry_out, and_3_out, and_5_out, and_6_out, and_7_out);
  or or_2 (Sum, and_1_out, and_2_out, and_4_out, and_7_out);

  // Notes on the sheet:
  //   1-Bit Adder 
  //   Iho López Tobi
  //   June 1st 2019
endmodule

module _1_Bit_ALU_Version_3 (
  input  Ainvert,
  input  Binvert,
  input  Carry_in,
  input  Operation,
  input  A,
  input  B,
  input  less,
  output Result,
  output out_9
);

  wire and_1_out, n2_1_mux_1_out, n2_1_mux_2_out, n2_1_mux_3_out, not_1_out, not_2_out, or_1_out;

  not not_1 (not_1_out, A);
  _2_1_MUX u_2_1_mux_1 (.in_0(A), .in_1(not_1_out), .Select(Ainvert), .out(n2_1_mux_1_out));
  _2_1_MUX u_2_1_mux_2 (.in_0(B), .in_1(not_2_out), .Select(Binvert), .out(n2_1_mux_2_out));
  not not_2 (not_2_out, B);
  and and_1 (and_1_out, n2_1_mux_1_out, n2_1_mux_2_out);
  or or_1 (or_1_out, n2_1_mux_1_out, n2_1_mux_2_out);
  _2_1_MUX u_2_1_mux_3 (.in_0(n2_1_mux_1_out), .in_1(n2_1_mux_2_out), .Select(Carry_in), .out(n2_1_mux_3_out));
  _4_1_MUX u_4_1_mux_1 (
    .in_00(and_1_out), .in_01(or_1_out), .in_10(n2_1_mux_3_out), .in_11(less), .sel_0(Operation),
    .Sel_1(Operation), .out(Result));

  // Notes on the sheet:
  //   1-Bit Alu Version 3
  //   Iho Lopez Tobi
  //   July 1st 2019
  //   Carry out
endmodule

module Top_Bit_ALU (
  input  Ainvert,
  input  Binvert,
  input  Carry_in,
  input  Operation,
  input  A,
  input  B,
  input  less,
  output Result,
  output Set,
  output Overflow
);

  wire and_1_out, n2_1_mux_1_out, n2_1_mux_2_out, n2_1_mux_3_out, not_1_out, not_2_out, or_1_out, undriven;

  not not_1 (not_1_out, A);
  _2_1_MUX u_2_1_mux_1 (.in_0(A), .in_1(not_1_out), .Select(Ainvert), .out(n2_1_mux_1_out));
  _2_1_MUX u_2_1_mux_2 (.in_0(B), .in_1(not_2_out), .Select(Binvert), .out(n2_1_mux_2_out));
  not not_2 (not_2_out, B);
  and and_1 (and_1_out, n2_1_mux_1_out, n2_1_mux_2_out);
  or or_1 (or_1_out, n2_1_mux_1_out, n2_1_mux_2_out);
  _2_1_MUX u_2_1_mux_3 (.in_0(n2_1_mux_1_out), .in_1(n2_1_mux_2_out), .Select(Carry_in), .out(n2_1_mux_3_out));
  _4_1_MUX u_4_1_mux_1 (
    .in_00(and_1_out), .in_01(or_1_out), .in_10(n2_1_mux_3_out), .in_11(less), .sel_0(Operation),
    .Sel_1(Operation), .out(Result));
  xor xor_1 (Set, n2_1_mux_3_out, Overflow);
  xor xor_2 (Overflow, undriven, n2_1_mux_2_out);

  // Notes on the sheet:
  //   Top-Bit ALU
  //   Iho Lopez Tobi
  //   July 1st 2019
endmodule

module _8_Bit_ALU_Version (
  input  Ainvert,
  input  Binvert,
  input  carry_in,
  input  operation,
  input  [7:0] in_5,
  input  [7:0] in_6,
  input  [7:0] in_7,
  output overflow
);

  wire n1_bit_alu_version_3_1_out_9, n1_bit_alu_version_3_2_out_9, n1_bit_alu_version_3_3_out_9,
       n1_bit_alu_version_3_4_out_9, n1_bit_alu_version_3_5_out_9, n1_bit_alu_version_3_6_out_9,
       n1_bit_alu_version_3_7_out_9, top_bit_alu_1_set;
  wire [7:0] n1_bit_alu_version_3_1_result;

  _1_Bit_ALU_Version_3 u_1_bit_alu_version_3_1 (
    .A(in_5[0]), .B(in_7[0]), .less(top_bit_alu_1_set), .Ainvert(Ainvert), .Binvert(Binvert),
    .Carry_in(carry_in), .Operation(operation), .out_9(n1_bit_alu_version_3_1_out_9),
    .Result(n1_bit_alu_version_3_1_result[0]));
  _1_Bit_ALU_Version_3 u_1_bit_alu_version_3_2 (
    .A(in_5[1]), .B(in_7[1]), .less(in_7[4]), .Ainvert(top_bit_alu_1_set), .Binvert(Ainvert),
    .Carry_in(n1_bit_alu_version_3_1_out_9), .Operation(operation), .out_9(n1_bit_alu_version_3_2_out_9),
    .Result(n1_bit_alu_version_3_1_result[1]));
  _1_Bit_ALU_Version_3 u_1_bit_alu_version_3_3 (
    .A(in_5[2]), .B(in_7[2]), .less(top_bit_alu_1_set), .Ainvert(in_7[4]), .Binvert(Ainvert),
    .Carry_in(n1_bit_alu_version_3_2_out_9), .Operation(operation), .out_9(n1_bit_alu_version_3_3_out_9),
    .Result(n1_bit_alu_version_3_1_result[2]));
  _1_Bit_ALU_Version_3 u_1_bit_alu_version_3_4 (
    .A(in_5[3]), .B(in_7[3]), .less(top_bit_alu_1_set), .Ainvert(in_7[4]), .Binvert(Ainvert),
    .Carry_in(n1_bit_alu_version_3_3_out_9), .Operation(operation), .out_9(n1_bit_alu_version_3_4_out_9),
    .Result(n1_bit_alu_version_3_1_result[3]));
  _1_Bit_ALU_Version_3 u_1_bit_alu_version_3_5 (
    .A(in_5[4]), .B(in_7[4]), .less(top_bit_alu_1_set), .Ainvert(in_7[4]), .Binvert(Ainvert),
    .Carry_in(n1_bit_alu_version_3_4_out_9), .Operation(operation), .out_9(n1_bit_alu_version_3_5_out_9),
    .Result(n1_bit_alu_version_3_1_result[4]));
  _1_Bit_ALU_Version_3 u_1_bit_alu_version_3_6 (
    .A(in_5[5]), .B(in_7[5]), .less(top_bit_alu_1_set), .Ainvert(in_7[4]), .Binvert(Ainvert),
    .Carry_in(n1_bit_alu_version_3_5_out_9), .Operation(operation), .out_9(n1_bit_alu_version_3_6_out_9),
    .Result(n1_bit_alu_version_3_1_result[5]));
  _1_Bit_ALU_Version_3 u_1_bit_alu_version_3_7 (
    .A(in_5[6]), .B(in_7[6]), .less(top_bit_alu_1_set), .Ainvert(in_7[4]), .Binvert(Ainvert),
    .Carry_in(n1_bit_alu_version_3_6_out_9), .Operation(operation), .out_9(n1_bit_alu_version_3_7_out_9),
    .Result(n1_bit_alu_version_3_1_result[6]));
  Top_Bit_ALU top_bit_alu_1 (
    .A(in_5[7]), .B(in_7[7]), .less(in_7[4]), .Ainvert(Ainvert), .Binvert(Binvert),
    .Carry_in(n1_bit_alu_version_3_7_out_9), .Operation(operation),
    .Result(n1_bit_alu_version_3_1_result[7]), .Set(top_bit_alu_1_set), .Overflow(overflow));

  // Notes on the sheet:
  //   8-Bit ALU
  //   Iho Lopez Tobi
  //   July 3rd 2019
  //   0
  //   Result
endmodule
