// Logisim project ProductSumTest.circ as structural Verilog: 1 circuit, main circuit main
module main (
  input  A,
  input  B,
  input  C,
  output out_4,
  output Product_of_Sums
);

  wire and_1_out, and_2_out, and_3_out, not_1_out, not_2_out, not_3_out, or_1_out, or_2_out, or_3_out;

  not not_1 (not_1_out, A);
  not not_2 (not_2_out, B);
  not not_3 (not_3_out, C);
  and and_1 (and_1_out, A, B, not_3_out);
  and and_2 (and_2_out, A, not_2_out, C);
  and and_3 (and_3_out, not_1_out, B, C);
  or or_1 (or_1_out, A, not_2_out, not_3_out);
  or or_2 (or_2_out, not_1_out, B, not_3_out);
  or or_3 (or_3_out, not_1_out, not_2_out, C);
  or or_4 (out_4, and_1_out, and_2_out, and_3_out);
  and and_4 (Product_of_Sums, or_1_out, or_2_out, or_3_out);

  // Notes on the sheet:
  //   Sum of Products
  //   Iho Lopez Tobi
  //   July 2nd 2019
endmodule
