// Logisim project ProductSumTest2.circ as structural Verilog: 1 circuit, main circuit main
module main (
  input  A,
  input  B,
  input  C,
  output out_4,
  output Product_of_Sums,
  output out_6,
  output out_7
);

  wire and_1_out, and_2_out, and_3_out, and_4_out, and_5_out, and_6_out, nand_1_out, not_1_out, not_2_out,
       not_3_out, or_1_out, or_2_out, or_3_out, or_4_out, xnor_1_out;

  not not_1 (not_1_out, A);
  not not_2 (not_2_out, B);
  not not_3 (not_3_out, C);
  and and_1 (and_1_out, A, B, not_3_out);
  and and_2 (and_2_out, A, not_2_out, C);
  and and_3 (and_3_out, not_1_out, B, C);
  or or_1 (or_1_out, A, not_2_out, not_3_out);
  or or_2 (or_2_out, not_1_out, B, not_3_out);
  or or_3 (or_3_out, not_1_out, not_2_out, C);
  or or_4 (or_4_out, A, B, C);
  nand nand_1 (nand_1_out, A, B, C);
  and and_4 (and_4_out, A, B);
  and and_5 (and_5_out, A, C);
  and and_6 (and_6_out, B, C);
  or or_5 (out_4, and_1_out, and_2_out, and_3_out);
  and and_7 (Product_of_Sums, or_1_out, or_2_out, or_3_out);
  NotExactlyOne xnor_1 (.out(xnor_1_out), .in0(A), .in1(B), .in2(C));
  and and_8 (out_6, xnor_1_out, or_4_out, nand_1_out);
  ExactlyOne xor_1 (.out(out_7), .in0(and_4_out), .in1(and_5_out), .in2(and_6_out));

  // Notes on the sheet:
  //   Sum of Products
  //   Iho Lopez Tobi
  //   July 2nd 2019
  //   E=(A&B)^(A&C)^(B&C)
  //   E=~(A^B^C)&(AlBlC)&~(A&b&C)
endmodule
