// Logisim project Revised MUX.circ as structural Verilog: 3 circuits, main circuit main
module main (
  input  X,
  input  Y,
  output out_3
);

  wire and_1_out, and_2_out, not_1_out, not_2_out;

  not not_1 (not_1_out, X);
  not not_2 (not_2_out, Y);
  and and_1 (and_1_out, not_1_out, Y);
  and and_2 (and_2_out, X, not_2_out);
  or or_1 (out_3, and_1_out, and_2_out);

  // Notes on the sheet:
  //   Iho López Tobi
  //   XOR circuit
  //   June 29th 2019
endmodule

module _2_1_MUX (
  input  Select,
  input  in_0,
  input  in_1,
  output out
);

  wire and_1_out, and_2_out, not_1_out;

  not not_1 (not_1_out, Select);
  and and_1 (and_1_out, in_0, not_1_out);
  and and_2 (and_2_out, in_1, Select);
  or or_1 (out, and_1_out, and_2_out);

  // Notes on the sheet:
  //   Revised
  //   2:1 MUX
  //   Iho Lopez Tobi
  //   June 29th 2019
endmodule

module _4_1_MUX (
  input  sel_0,
  input  Sel_1,
  input  in_00,
  input  in_01,
  input  in_10,
  input  in_11,
  output out
);

  wire n2_1_mux_1_out, n2_1_mux_2_out;

  _2_1_MUX u_2_1_mux_1 (.in_0(in_00), .in_1(in_01), .Select(Sel_1), .out(n2_1_mux_1_out));
  _2_1_MUX u_2_1_mux_2 (.in_0(in_10), .in_1(in_11), .Select(Sel_1), .out(n2_1_mux_2_out));
  _2_1_MUX u_2_1_mux_3 (.in_0(n2_1_mux_1_out), .in_1(n2_1_mux_2_out), .Select(sel_0), .out(out));

  // Notes on the sheet:
  //   Iho Lopez Tobi
  //   June 29th 2019
  //   Revised 4:1 MUX
endmodule
